# Fritzing sketch ModuloPrincipal (saved by Fritzing 0.8.7b)
circuit board: 7.98715cm x 8.73953cm
breadboards: 1

parts:
  P8 = 46 Pins Beagle [form="♂ (male)" package=THT]  # not connected
  P9 = 46 Pins Beagle [form="♂ (male)" package=THT]
  U1 = Voltage Regulator - 5V [package="TO220 [THT]"]
  C1 = Electrolytic Capacitor [capacitance=220µF voltage=16V package="100 mil [THT, electrolytic]"]
  C2 = Electrolytic Capacitor [capacitance=33µF package="100 mil [THT, electrolytic]"]
  C3 = Ceramic Capacitor [capacitance=0.1µF package="100 mil [THT, multilayer]"]
  C4 = Ceramic Capacitor [capacitance=0.1µF package="100 mil [THT, multilayer]"]
  J1 = female pin header, 2 pins [form="♀ (female)"]
  D1 = Diode [package=diode-1n4001]
  CD4051B = IC, DIP package, 16 pins [chip_label=CD4051B]
  J2 = female pin header, 14 pins [form="♀ (female)"]
  J3 = female pin header, 14 pins [form="♀ (female)"]
  J4 = female pin header, 14 pins [form="♀ (female)"]

nets:
  GND: P9.pin1, P9.pin2, P9.pin43, P9.pin44, P9.pin45, P9.pin46, U1.GND, C1.-, C2.-, C3.0, C4.0, J1.pin2
  3.3V: P9.pin3, P9.pin4, CD4051B.pin16
  5V: P9.pin5, P9.pin6, U1.output_voltage, C2.+, C4.1
  N1: P9.pin27, CD4051B.pin11
  N2: P9.pin30, CD4051B.pin10
  N3: P9.pin32, J3.pin1, J3.pin2, J3.pin3, J3.pin4, J3.pin5, J3.pin6, J3.pin7, J3.pin8, J3.pin9, J3.pin10, J3.pin11, J3.pin12, J3.pin13, J3.pin14
  N4: P9.pin33, J2.pin5
  N5: P9.pin34, CD4051B.pin6, CD4051B.pin7, CD4051B.pin8, J4.pin1, J4.pin2, J4.pin3, J4.pin4, J4.pin5, J4.pin6, J4.pin7, J4.pin8, J4.pin9, J4.pin10, J4.pin11, J4.pin12, J4.pin13, J4.pin14
  N6: P9.pin35, CD4051B.pin3
  N7: P9.pin36, J2.pin6
  N8: P9.pin37, J2.pin3
  N9: P9.pin38, J2.pin4
  N10: P9.pin39, J2.pin1
  N11: P9.pin40, J2.pin2
  N12: P9.pin42, CD4051B.pin9
  N13: U1.input_voltage, C1.+, C3.1, D1.C
  N14: J1.pin1, D1.A
  N15: CD4051B.pin1, J2.pin11
  N16: CD4051B.pin2, J2.pin13
  N17: CD4051B.pin4, J2.pin14
  N18: CD4051B.pin5, J2.pin12
  N19: CD4051B.pin12, J2.pin10
  N20: CD4051B.pin13, J2.pin7
  N21: CD4051B.pin14, J2.pin8
  N22: CD4051B.pin15, J2.pin9

custom parts:
  46 Pins Beagle: 46 pins beagle
